// Logisim project NANDToCPU.circ as structural Verilog
module half_adder (
  input  in_1,
  input  in_2,
  output out_3,
  output out_4
);

  and and_1 (out_3, in_1, in_2);
  xor xor_1 (out_4, in_1, in_2);
endmodule

module Full_Adder (
  input  A,
  input  B,
  input  Carry,
  output C_Out,
  output Sum
);

  wire and_1_out, half_adder_1_out_3, half_adder_1_out_4;

  half_adder half_adder_1 (.in_1(B), .in_2(Carry), .out_3(half_adder_1_out_3), .out_4(half_adder_1_out_4));
  and and_1 (and_1_out, A, half_adder_1_out_4);
  xor xor_1 (Sum, A, half_adder_1_out_4);
  xor xor_2 (C_Out, and_1_out, half_adder_1_out_3);
endmodule

module _4_Bit_Adder (
  input  [3:0] in_1,
  input  [3:0] in_2,
  output out_3,
  output [3:0] out_4
);

  wire full_adder_1_c_out, full_adder_2_c_out, full_adder_3_c_out;

  Full_Adder full_adder_1 (.A(in_1[0]), .B(in_2[0]), .Carry(1'b0), .C_Out(full_adder_1_c_out), .Sum(out_4[0]));
  Full_Adder full_adder_2 (
    .A(in_1[1]), .B(in_2[1]), .Carry(full_adder_1_c_out), .C_Out(full_adder_2_c_out), .Sum(out_4[1]));
  Full_Adder full_adder_3 (
    .A(in_2[2]), .B(in_1[2]), .Carry(full_adder_2_c_out), .C_Out(full_adder_3_c_out), .Sum(out_4[2]));
  Full_Adder full_adder_4 (.A(in_2[3]), .B(in_1[3]), .Carry(full_adder_3_c_out), .C_Out(out_3), .Sum(out_4[3]));
endmodule

module _16_Bit_Adder__2 (
  input  in_1,
  input  [15:0] A,
  input  [15:0] B,
  output out_4,
  output [15:0] Sum
);

  wire full_adder_1_c_out, full_adder_2_c_out, full_adder_3_c_out, full_adder_4_c_out, full_adder_5_c_out,
       full_adder_6_c_out, full_adder_7_c_out, full_adder_8_c_out, full_adder_9_c_out, full_adder_10_c_out,
       full_adder_11_c_out, full_adder_12_c_out, full_adder_13_c_out, full_adder_14_c_out,
       full_adder_15_c_out;

  Full_Adder full_adder_1 (.A(A[0]), .B(B[0]), .Carry(in_1), .C_Out(full_adder_1_c_out), .Sum(Sum[0]));
  Full_Adder full_adder_2 (.A(A[1]), .B(B[1]), .Carry(full_adder_1_c_out), .C_Out(full_adder_2_c_out), .Sum(Sum[1]));
  Full_Adder full_adder_3 (.A(A[2]), .B(B[2]), .Carry(full_adder_2_c_out), .C_Out(full_adder_3_c_out), .Sum(Sum[2]));
  Full_Adder full_adder_4 (.A(A[3]), .B(B[3]), .Carry(full_adder_3_c_out), .C_Out(full_adder_4_c_out), .Sum(Sum[3]));
  Full_Adder full_adder_5 (.A(A[4]), .B(B[4]), .Carry(full_adder_4_c_out), .C_Out(full_adder_5_c_out), .Sum(Sum[4]));
  Full_Adder full_adder_6 (.A(A[5]), .B(B[5]), .Carry(full_adder_5_c_out), .C_Out(full_adder_6_c_out), .Sum(Sum[5]));
  Full_Adder full_adder_7 (.A(A[6]), .B(B[6]), .Carry(full_adder_6_c_out), .C_Out(full_adder_7_c_out), .Sum(Sum[6]));
  Full_Adder full_adder_8 (.A(A[7]), .B(B[7]), .Carry(full_adder_7_c_out), .C_Out(full_adder_8_c_out), .Sum(Sum[7]));
  Full_Adder full_adder_9 (.A(A[8]), .B(B[8]), .Carry(full_adder_8_c_out), .C_Out(full_adder_9_c_out), .Sum(Sum[8]));
  Full_Adder full_adder_10 (.A(A[9]), .B(B[9]), .Carry(full_adder_9_c_out), .C_Out(full_adder_10_c_out), .Sum(Sum[9]));
  Full_Adder full_adder_11 (
    .A(A[10]), .B(B[10]), .Carry(full_adder_10_c_out), .C_Out(full_adder_11_c_out), .Sum(Sum[10]));
  Full_Adder full_adder_12 (
    .A(A[11]), .B(B[11]), .Carry(full_adder_11_c_out), .C_Out(full_adder_12_c_out), .Sum(Sum[11]));
  Full_Adder full_adder_13 (
    .A(A[12]), .B(B[12]), .Carry(full_adder_12_c_out), .C_Out(full_adder_13_c_out), .Sum(Sum[12]));
  Full_Adder full_adder_14 (
    .A(A[13]), .B(B[13]), .Carry(full_adder_13_c_out), .C_Out(full_adder_14_c_out), .Sum(Sum[13]));
  Full_Adder full_adder_15 (
    .A(A[14]), .B(B[14]), .Carry(full_adder_14_c_out), .C_Out(full_adder_15_c_out), .Sum(Sum[14]));
  Full_Adder full_adder_16 (.A(A[15]), .B(B[15]), .Carry(full_adder_15_c_out), .C_Out(out_4), .Sum(Sum[15]));
endmodule

module Increment_16_Bit (
  input  [15:0] in_1,
  output [15:0] out_2,
  output out_3
);

  _16_Bit_Adder__2 u_16_bit_adder_2_1 (.Sum(out_2), .A(in_1), .B(16'h1), .out_4(out_3), .in_1(1'b0));
endmodule

module _16_Bit_Subtracter (
  input  [15:0] in_1,
  input  [15:0] in_2,
  output out_3,
  output [15:0] out_4
);

  wire increment_16_bit_1_out_3;
  wire [15:0] increment_16_bit_1_out_2, not_1_out;

  assign not_1_out = ~in_2;  // NOT_Gate not_1, 16 bits wide
  Increment_16_Bit increment_16_bit_1 (
    .in_1(not_1_out), .out_2(increment_16_bit_1_out_2), .out_3(increment_16_bit_1_out_3));
  _16_Bit_Adder__2 u_16_bit_adder_2_1 (
    .Sum(out_4), .A(in_1), .B(increment_16_bit_1_out_2), .out_4(out_3), .in_1(increment_16_bit_1_out_3));
endmodule

module _16_Bit_Equal_to_Zero (
  input  [15:0] in_1,
  output out_2
);

  wire or_1_out, or_2_out, or_3_out, or_4_out, or_5_out, or_6_out, or_7_out, or_8_out, or_9_out, or_10_out,
       or_11_out, or_12_out, or_13_out, or_14_out, or_15_out;

  or or_1 (or_1_out, in_1[0], in_1[1]);
  or or_2 (or_2_out, in_1[2], in_1[3]);
  or or_3 (or_3_out, in_1[4], in_1[5]);
  or or_4 (or_4_out, in_1[6], in_1[7]);
  or or_5 (or_5_out, in_1[8], in_1[9]);
  or or_6 (or_6_out, in_1[10], in_1[11]);
  or or_7 (or_7_out, in_1[12], in_1[13]);
  or or_8 (or_8_out, in_1[14], in_1[15]);
  or or_9 (or_9_out, or_1_out, or_2_out);
  or or_10 (or_10_out, or_3_out, or_4_out);
  or or_11 (or_11_out, or_5_out, or_6_out);
  or or_12 (or_12_out, or_7_out, or_8_out);
  or or_13 (or_13_out, or_9_out, or_10_out);
  or or_14 (or_14_out, or_11_out, or_12_out);
  or or_15 (or_15_out, or_13_out, or_14_out);
  not not_1 (out_2, or_15_out);
endmodule

module _16_Bit_Less_than_Zero (
  input  [15:0] in_1,
  output out_2
);


  assign out_2 = in_1[15];
endmodule

module Selector (
  input  Data_1,
  input  Data_0,
  input  Select,
  output Output
);

  wire and_1_out, and_2_out, not_1_out;

  not not_1 (not_1_out, Select);
  and and_1 (and_1_out, Data_1, Select);
  and and_2 (and_2_out, not_1_out, Data_0);
  or or_1 (Output, and_1_out, and_2_out);
endmodule

module Switch (
  input  Data,
  input  Select,
  output _1,
  output _0
);

  wire not_1_out;

  not not_1 (not_1_out, Select);
  and and_1 (_1, Data, Select);
  and and_2 (_0, Data, not_1_out);
endmodule

module Latch (
  input  Data,
  input  Store,
  output out_3
);

  Selector selector_1 (.Data_1(Data), .Data_0(out_3), .Select(Store), .Output(out_3));
endmodule
